# Fritzing sketch encoder_speed (saved by Fritzing 0.9.3b)

parts:
  Componente1 = Arduino Uno (Rev3)
  SW2 = ENCODER_RGB_CA [package=encoder_led_3]

nets:
  N1: Componente1.D8, SW2.-B
  N2: Componente1.D6_PWM, SW2.A
  N3: Componente1.D7, SW2.+
  N4: Componente1.5V, SW2.B
  N5: Componente1.GND, SW2.C
