# Fritzing sketch encoder_speed2 (saved by Fritzing 0.9.3b)

parts:
  Componente1 = Arduino Uno (Rev3)
  RE1 = Rotary Encoder [package=THT]

nets:
  N1: Componente1.D8, RE1.EncoderPinA
  N2: Componente1.GND, RE1.EncoderPinC
  N3: Componente1.D7, RE1.EncoderPinB
