# Fritzing sketch indicador_rumbo (saved by Fritzing 0.9.3b)

parts:
  Componente1 = Arduino Uno (Rev3)
  RE1 = Rotary Encoder [package=THT]
  RE2 = Rotary Encoder [package=THT]

nets:
  N1: Componente1.D8, RE2.EncoderPinB
  N2: Componente1.D9_PWM, RE2.EncoderPinA
  N3: Componente1.GND, RE1.EncoderPinC, RE2.EncoderPinC
  N4: Componente1.D6_PWM, RE1.EncoderPinB
  N5: Componente1.D7, RE1.EncoderPinA
