# Fritzing sketch magnetos (saved by Fritzing 0.9.3b)

parts:
  Componente1 = Arduino Uno (Rev3)
  switch1 = Rotary Switch 2x6

nets:
  N1: Componente1.D8, switch1.1
  N2: Componente1.D9_PWM, switch1.2
  N3: Componente1.D10_PWM/SS, switch1.3
  N4: Componente1.D11_PWM/MOSI, switch1.4
  N5: Componente1.D12/MISO, switch1.5
  N6: Componente1.GND, switch1.C

custom parts:
  Rotary Switch 2x6: Rotary Switch 2x6 - 2 pole 6 position - DP6T Knob arrow will point as per drawing when in position #1
